# Fritzing sketch Untitled Sketch (saved by Fritzing 0.9.3b)

parts:
  Power_plug1 = Power plug
  RFM95W1 = RFM95W LoRa Module
  U1 = ESP8266 NodeMCU LoLin module
  M1 = NEO-6M GPS Module [part_number=GY-GPS6MV2]
  U2 = LM2596 step down module
  C1 = Electrolytic Capacitor [capacitance=100µF package="200 mil [THT, electrolytic]"]

nets:
  GND: Power_plug1.GND, RFM95W1.10_GND, U1.GND, M1.GND, U2.IN-, U2.OUT-, C1.-
  N1: Power_plug1.VCC, U2.IN+
  N2: RFM95W1.2_MISO, U1.D6
  N3: RFM95W1.3_MOSI, U1.D7
  N4: RFM95W1.4_SCK, U1.D5
  N5: RFM95W1.5_NSS_(CS), U1.D8
  N6: RFM95W1.6_RESET, U1.D0, U1.RX, M1.Tx
  N7: RFM95W1.13_3.3V, U1.3V3
  N8: RFM95W1.14_DIO0, U1.D2
  N9: RFM95W1.15_DIO1, U1.D1
  N10: U1.TX, M1.Rx
  VIN: U1.Vin, M1.Vcc, U2.OUT+, C1.+

custom parts:
  Power plug: 秋月電子通商 AE-DCJACK-DIPKIT-2.1mm-10A(通販コードK-06998)とその互換品(K06999,K-08415,K-08416)
  RFM95W LoRa Module: RF Transceiver by Hope RF. Well supported Arduino libraries are available. This Low Power Long Range Transceiver Module for the frequencies 868MHz and 915MHz and it is also available in other versions.
  ESP8266 NodeMCU LoLin module: ESP8266 based NodeMCU
  NEO-6M GPS Module: GY-GPS6MV2 NEO-6M GPS Module Module based on U-blox NEO-6M GPS engine, incorporating regulator for 3.3-5V DC input, MS621FE-compatible rechargeable battery for backup and EEPROM for storing configuration settings. Links: NEO-6 series product information page NEO-6 Datasheet
  LM2596 step down module: LM2596 DC-DC step down power supply module 3 A.
